# Fritzing sketch gsync_circuit (saved by Fritzing 0.9.3b)
breadboards: 1

parts:
  BeagleBone1 = BeagleBone Black
  BeagleBone2 = BeagleBone Black
  R1 = Resistor [tolerance=±5% resistance=470 package="0603 [SMD]"]
  LED1 = LED - 5mm [color="Green (565nm)" package="5 mm [THT]"]
  R2 = Resistor [tolerance=±5% resistance=470 package=THT]
  LED2 = LED - 5mm [color="Green (565nm)" package="5 mm [THT]"]

nets:
  N1: BeagleBone1.no_name_yet#1, BeagleBone1.no_name_yet#2, BeagleBone2.no_name_yet#2, LED1.cathode, LED2.cathode
  N2: BeagleBone1.no_name_yet#15, R2.Pin_1, LED2.anode
  N3: BeagleBone1.no_name_yet#23, R1.Pin_1, LED1.anode
  N4: BeagleBone2.no_name_yet#15, BeagleBone2.no_name_yet#16, R1.Pin_0
  N5: BeagleBone2.no_name_yet#23, BeagleBone2.no_name_yet#24, R2.Pin_0

custom parts:
  BeagleBone Black: BeagleBone Black rev. A5B
